# Fritzing sketch lidar-pcb (saved by Fritzing 0.9.3b)
breadboards: 1

parts:
  J1 = screw terminal, 6 pins  # not connected
  Part1 = Arduino Nano (Rev3.0) (ICSP)
  Pololu_A1 = Pololu A4988 [package=SO16]  # not connected

nets:
  N1: Part1.A5, Part1.A4
